// Logisim project Additionneur.circ as structural Verilog
module Add (
  input  a,
  input  b,
  output S,
  output C
);

  Adder #(.width(1)) adder_1 (.a(a), .b(b), .out(S), .cout(C));  // open: cin
endmodule

module add_complet (
  input  a,
  input  b,
  input  ci,
  output S,
  output Co
);

  wire adder_1_cout, adder_1_out, adder_2_cout;

  Adder #(.width(1)) adder_1 (.a(a), .b(b), .out(adder_1_out), .cout(adder_1_cout));  // open: cin
  Adder #(.width(1)) adder_2 (.a(adder_1_out), .b(ci), .out(S), .cout(adder_2_cout));  // open: cin
  or or_1 (Co, adder_2_cout, adder_1_cout);
endmodule

module Add_Prog (
  input  in_1,
  input  [1:0] in_2,
  input  [1:0] in_3,
  output [2:0] out_4
);

  wire adder_1_cout;

  Adder #(.width(1)) adder_1 (.a(in_2[0]), .b(in_2[1]), .out(out_4[0]), .cin(in_1), .cout(adder_1_cout));
  Adder #(.width(1)) adder_2 (.a(in_2[1]), .b(in_2[1]), .out(out_4[1]), .cin(adder_1_cout), .cout(out_4[2]));

  assign in_3 = {2{in_2[1]}};
endmodule
