// Logisim project ComparateurNonSigne.circ as structural Verilog: 1 circuit, main circuit main
module main (
  input  a0,
  input  a1,
  input  b0,
  input  b1,
  output inf
);

  wire and_1_out, and_2_out, and_3_out, not_1_out, not_2_out;

  not not_1 (not_1_out, a0);
  not not_2 (not_2_out, a1);
  and and_1 (and_1_out, not_1_out, not_2_out, b1);
  and and_2 (and_2_out, not_1_out, b0);
  and and_3 (and_3_out, not_2_out, b0, b1);
  or or_1 (inf, and_1_out, and_2_out, and_3_out);
endmodule
