// Logisim project MIPS-ENONCE.circ as structural Verilog
module DECODEUR_CO (
  input  [5:0] Co,
  output zero,
  output ijal,
  output ibeq,
  output ibne,
  output ilbu,
  output iaddiu,
  output islti,
  output iandi,
  output ixori,
  output isltiu,
  output iori,
  output ilui,
  output isb
);

  wire decoder_1_out0, decoder_1_out1, decoder_1_out4, decoder_1_out5;

  Decoder #(.enable("false"), .select(3)) decoder_1 (
    .out0(decoder_1_out0), .out1(decoder_1_out1), .out4(decoder_1_out4), .out5(decoder_1_out5), .sel(Co[5:3]));  // open: out2, out3, out6, out7
  Decoder #(.select(3)) decoder_2 (
    .out0(zero), .out3(ijal), .out4(ibeq), .out5(ibne), .sel(Co[2:0]), .en(decoder_1_out0));  // open: out1, out2, out6, out7
  Decoder #(.select(3)) decoder_3 (
    .out1(iaddiu), .out2(islti), .out3(isltiu), .out4(iandi), .out5(iori), .out6(ixori), .out7(ilui),
    .sel(Co[2:0]), .en(decoder_1_out1));  // open: out0
  Decoder #(.select(3)) decoder_4 (
    .out5(ilbu), .sel(Co[2:0]), .en(decoder_1_out4));  // open: out0, out1, out2, out3, out4, out6, out7
  Decoder #(.select(3)) decoder_5 (
    .out0(isb), .sel(Co[2:0]), .en(decoder_1_out5));  // open: out1, out2, out3, out4, out5, out6, out7
endmodule

module DECODEUR_NF (
  input  en,
  input  [5:0] Nf,
  output isll,
  output isrl,
  output isllv,
  output isrlv,
  output isra,
  output israv,
  output ijr,
  output iaddu,
  output isubu,
  output ior,
  output iand,
  output ixor,
  output inor,
  output islt,
  output isltu
);

  wire decoder_1_out0, decoder_1_out1, decoder_1_out4, decoder_1_out5;

  Decoder #(.select(3)) decoder_1 (
    .out0(decoder_1_out0), .out1(decoder_1_out1), .out4(decoder_1_out4), .out5(decoder_1_out5),
    .sel(Nf[5:3]), .en(en));  // open: out2, out3, out6, out7
  Decoder #(.select(3)) decoder_2 (
    .out0(isll), .out2(isrl), .out3(isra), .out4(isllv), .out6(isrlv), .out7(israv), .sel(Nf[2:0]),
    .en(decoder_1_out0));  // open: out1, out5
  Decoder #(.select(3)) decoder_3 (
    .out0(ijr), .en(decoder_1_out1));  // open: out1, out2, out3, out4, out5, out6, out7, sel
  Decoder #(.select(3)) decoder_4 (
    .out1(iaddu), .out3(isubu), .out4(iand), .out5(ior), .out6(ixor), .out7(inor), .en(decoder_1_out4));  // open: out0, out2, sel
  Decoder #(.select(3)) decoder_5 (
    .out2(islt), .out3(isltu), .sel(Nf[2:0]), .en(decoder_1_out5));  // open: out0, out1, out4, out5, out6, out7
endmodule

module ENCODEUR (
  input  e0,
  input  e1,
  input  e2,
  input  e3,
  input  e4,
  input  e5,
  input  e6,
  input  e7,
  input  e8,
  input  e9,
  input  e10,
  input  e11,
  output [3:0] s3_0
);

  or or_1 (s3_0[0], e1, e3, e5, e7, e9, e11);
  or or_2 (s3_0[1], e2, e3, e6, e7, e10, e11);
  or or_3 (s3_0[2], e4, e5, e6, e7);
  or or_4 (s3_0[3], e8, e9, e10, e11);
endmodule

module ZERO (
  input  [31:0] e,
  output eqZero
);

  not not_1 (eqZero, e[31]);
endmodule

module CMD (
  input  [5:0] Co,
  input  [5:0] Nf,
  output sjal,
  output sbeq,
  output sbne,
  output [3:0] Op,
  output sjr,
  output slbu,
  output ssb,
  output smx1,
  output sNs,
  output sShamt,
  output serg
);

  wire iaddiu, iaddu, iand, iandi, ilui, inor, ior, iori, isll, isllv, islt, islti, isltiu, isltu, isra,
       israv, isrl, isrlv, isubu, ixor, ixori, opET, opLUI, opNOU, opOU, opPLUS, opSLL, opSLT, opSLTU, opSRA,
       opSRL, opSUB, opXOU, undriven, undriven_2, undriven_3, undriven_4, undriven_5, undriven_6, undriven_7,
       undriven_8, undriven_9, undriven_10, undriven_11, undriven_12, undriven_13, undriven_14, undriven_15,
       undriven_16, undriven_17, undriven_18, undriven_19, undriven_20, undriven_21, undriven_22,
       undriven_23, undriven_24, undriven_25, undriven_26, undriven_27, undriven_28, undriven_29,
       undriven_30, undriven_31, undriven_32, undriven_33, undriven_34, undriven_35, undriven_36,
       undriven_37, zero;

  or or_1 (smx1, undriven_4, undriven_5, undriven_6);
  or or_2 (sNs, undriven_7, undriven_8, undriven_9);
  or or_3 (sShamt, undriven_10, undriven_11, undriven_12);
  nor nor_1 (serg, undriven, undriven_2, undriven_3, undriven_13);
  DECODEUR_CO decodeur_co_1 (
    .Co(Co), .zero(zero), .ijal(sjal), .ibeq(sbeq), .ibne(sbne), .ilbu(iaddiu), .iaddiu(islti),
    .islti(isltiu), .iandi(iandi), .ixori(iori), .isltiu(ixori), .iori(ilui), .ilui(slbu), .isb(ssb));
  or or_4 (opPLUS, undriven_16, undriven_14, undriven_22, undriven_23, undriven_24);
  or or_5 (opET, undriven_17, undriven_18);
  or or_6 (opOU, undriven_15, undriven_19);
  or or_7 (opXOU, undriven_20, undriven_21);
  or or_8 (opSLL, undriven_26, undriven_27);
  or or_9 (opSRL, undriven_25, undriven_28);
  DECODEUR_NF decodeur_nf_1 (
    .en(zero), .Nf(Nf), .isll(isll), .isrl(isrl), .isllv(isra), .isrlv(isllv), .isra(isrlv), .israv(israv),
    .ijr(sjr), .iaddu(iaddu), .isubu(isubu), .ior(iand), .iand(ior), .ixor(ixor), .inor(inor), .islt(islt),
    .isltu(isltu));
  or or_10 (opSRA, undriven_29, undriven_30);
  or or_11 (opSUB, undriven_31, undriven_34, undriven_37);
  or or_12 (opSLT, undriven_32, undriven_33);
  or or_13 (opSLTU, undriven_35, undriven_36);
  ENCODEUR encodeur_1 (
    .e0(opPLUS), .e1(opET), .e2(opOU), .e3(opNOU), .e4(opXOU), .e5(opSLL), .e6(opSRL), .e7(opSRA),
    .e8(opSUB), .e9(opLUI), .e10(opSLT), .e11(opSLTU), .s3_0(Op));

  // Other names for the same wires on the sheet: ibeq = sbeq; ibne = sbne; ijr = sjr; ilbu = slbu; isb = ssb
endmodule

module UAL (
  input  [31:0] A,
  input  [31:0] B,
  input  [3:0] Op,
  output [31:0] S,
  output zero
);

  wire [31:0] adder_1_out, and_1_out;

  Adder #(.width(32)) adder_1 (.a(A), .b(B), .out(adder_1_out));  // open: cin, cout
  assign and_1_out = A & B;  // AND_Gate and_1, 32 bits wide
  Multiplexer #(.select(4), .width(32)) multiplexer_1 (
    .in0(adder_1_out), .in1(and_1_out), .in12({32{1'b0}}), .in13({32{1'b0}}), .in14({32{1'b0}}),
    .in15({32{1'b0}}), .out(S), .sel(Op));  // open: in2, in3, in4, in5, in6, in7, in8, in9, in10, in11
endmodule

module BANC_REG (
  input  [31:0] ValRw,
  input  H,
  input  [4:0] numRs,
  input  [4:0] numRt,
  input  ereg,
  input  [4:0] numRw,
  output [31:0] valRs,
  output [31:0] valRt,
  output [31:0] val_v0,
  output [31:0] val_v1,
  output [31:0] val_a0,
  output [31:0] val_a1,
  output [31:0] val_a2,
  output [31:0] val_a3,
  output [31:0] val_ra
);

  wire decoder_1_out2, decoder_1_out3, decoder_1_out4, decoder_1_out5, decoder_1_out6, decoder_1_out7,
       decoder_1_out31, n2, n3, n4, n5, n6, n7, n32;
  wire [31:0] undriven, undriven_2, undriven_3, undriven_4, undriven_5, undriven_6, undriven_7, undriven_8,
       undriven_9, undriven_10, undriven_11, undriven_12;

  Decoder #(.select(5)) decoder_1 (
    .out2(decoder_1_out2), .out3(decoder_1_out3), .out4(decoder_1_out4), .out5(decoder_1_out5),
    .out6(decoder_1_out6), .out7(decoder_1_out7), .out31(decoder_1_out31), .sel(numRw), .en(ereg));  // open: out0, out1, out8, out9, out10, out11, out12, out13, out14, out15, out16, out17, out18, out19, out20, out21, out22, out23, out24, out25, out26, out27, out28, out29, out30
  Register #(.width(32)) v0 (.D(ValRw), .en(n2), .Q(val_v0), .clk(H));  // open: clr
  Register #(.width(32)) v1 (.D(ValRw), .en(n3), .Q(val_v1), .clk(H));  // open: clr
  Register #(.width(32)) a0 (.D(ValRw), .en(n4), .Q(val_a0), .clk(H));  // open: clr
  Register #(.width(32)) a1 (.D(ValRw), .en(n5), .Q(val_a1), .clk(H));  // open: clr
  Register #(.width(32)) a2 (.D(ValRw), .en(n6), .Q(val_a2), .clk(H));  // open: clr
  Register #(.width(32)) a3 (.D(ValRw), .en(n7), .Q(val_a3), .clk(H));  // open: clr
  Register #(.width(32)) ra (.D(ValRw), .en(n32), .Q(val_ra), .clk(H));  // open: clr
  Multiplexer #(.select(5), .width(32)) multiplexer_1 (
    .in0({32{1'b0}}), .in2(undriven_4), .in3(undriven), .in4(undriven_5), .in5(undriven_2), .in6(undriven_6),
    .in7(undriven_3), .in31(val_ra), .out(valRs), .sel(numRs));  // open: in1, in8, in9, in10, in11, in12, in13, in14, in15, in16, in17, in18, in19, in20, in21, in22, in23, in24, in25, in26, in27, in28, in29, in30
  Multiplexer #(.select(5), .width(32)) multiplexer_2 (
    .in0({32{1'b0}}), .in2(undriven_10), .in3(undriven_7), .in4(undriven_11), .in5(undriven_8),
    .in6(undriven_12), .in7(undriven_9), .in31(val_ra), .out(valRt), .sel(numRt));  // open: in1, in8, in9, in10, in11, in12, in13, in14, in15, in16, in17, in18, in19, in20, in21, in22, in23, in24, in25, in26, in27, in28, in29, in30

  // Other names for the same wires on the sheet: a0[31:0] = val_a0; a1[31:0] = val_a1; a2[31:0] = val_a2;
  //   a3[31:0] = val_a3; ra[31:0] = val_ra; v0[31:0] = val_v0; v1[31:0] = val_v1
endmodule

module MIPS_SIMPLIFIE (
);

  wire and_1_out, and_2_out, and_3_out, and_4_out, C, comparator_1_eq, comparator_2_eq, comparator_3_eq,
       comparator_4_lt, keyboard_1_avail, mxBr, not_1_out, R, sbeq, sbne, sereg, sjal, sjr, slbu, smx1, sNs,
       ssb, sShamt, ual_1_zero;
  wire [2:0] undriven_2;
  wire [3:0] Op;
  wire [4:0] multiplexer_2_out, numRd, numRs, numRt;
  wire [5:0] Co, Nf;
  wire [6:0] keyboard_1_data;
  wire [7:6] undriven;
  wire [31:0] adder_1_out, adder_2_out, banc_reg_1_val_a0, banc_reg_1_val_a1, banc_reg_1_val_a2,
       banc_reg_1_val_a3, banc_reg_1_val_ra, banc_reg_1_val_v0, banc_reg_1_val_v1, banc_reg_1_valrs,
       bit_extender_1_out, bit_extender_2_out, immNs, immS, multiplexer_1_out, multiplexer_3_out,
       multiplexer_4_out, multiplexer_5_out, register_1_q, resUAL, Shamt, shifter_1_out, subtractor_1_out,
       valData, valMem, valRb;

  Clock clock_1 (.out(C));
  Shifter #(.width(32)) shifter_1 (.in(immS), .\dist (5'b00010), .out(shifter_1_out));
  Multiplexer #(.width(32)) multiplexer_1 (.in0(resUAL), .in1(valData), .out(multiplexer_1_out), .sel(slbu));
  Adder #(.width(32)) adder_1 (.a(register_1_q), .b(32'h4), .out(adder_1_out));  // open: cin, cout
  Adder #(.width(32)) adder_2 (.a(adder_1_out), .b(shifter_1_out), .out(adder_2_out));  // open: cin, cout
  Multiplexer #(.width(5)) multiplexer_2 (.in0(numRt), .in1(numRd), .out(multiplexer_2_out), .sel(smx1));
  Multiplexer #(.width(32)) multiplexer_3 (.in0(adder_1_out), .in1(adder_2_out), .out(multiplexer_3_out), .sel(mxBr));
  Comparator #(.mode("unsigned"), .width(32)) comparator_1 (
    .a(resUAL), .b(32'h7f0c), .eq(comparator_1_eq));  // open: gt, lt
  Comparator #(.mode("unsigned"), .width(32)) comparator_2 (
    .a(resUAL), .b(32'h7f04), .eq(comparator_2_eq));  // open: gt, lt
  Comparator #(.mode("unsigned"), .width(32)) comparator_3 (
    .a(resUAL), .b(32'h7f00), .eq(comparator_3_eq));  // open: gt, lt
  POR #(.PorHighDuration(1)) por_1 (.out(R));
  Subtractor #(.width(32)) subtractor_1 (.a(resUAL), .b(32'h2000), .out(subtractor_1_out));  // open: bin, bout
  Comparator #(.mode("unsigned"), .width(32)) comparator_4 (
    .a(subtractor_1_out), .b(32'h2000), .lt(comparator_4_lt));  // open: gt, eq
  Register #(.width(32)) register_1 (.D(multiplexer_3_out), .en(1'b1), .Q(register_1_q), .clk(not_1_out), .clr(R));
  not not_1 (not_1_out, C);
  BANC_REG banc_reg_1 (
    .ValRw(multiplexer_1_out), .H(C), .numRs(numRs), .numRt(numRt), .ereg(sereg), .numRw(multiplexer_2_out),
    .valRs(banc_reg_1_valrs), .valRt(valRb), .val_v0(banc_reg_1_val_v0), .val_v1(banc_reg_1_val_v1),
    .val_a0(banc_reg_1_val_a0), .val_a1(banc_reg_1_val_a1), .val_a2(banc_reg_1_val_a2),
    .val_a3(banc_reg_1_val_a3), .val_ra(banc_reg_1_val_ra));
  // Probe on banc_reg_1_val_v0
  // Probe on banc_reg_1_val_v1
  // Probe on banc_reg_1_val_a0
  // Probe on banc_reg_1_val_a1
  // Probe on banc_reg_1_val_a2
  // Probe on banc_reg_1_val_a3
  // Probe on banc_reg_1_val_ra
  and and_1 (and_1_out, comparator_4_lt, ssb);
  TTY tty_1 (.data(valRb[6:0]), .clk(C), .we(comparator_1_eq), .clr(R));
  and and_2 (and_2_out, C, comparator_2_eq);
  Keyboard keyboard_1 (.clk(and_2_out), .avail(keyboard_1_avail), .data(keyboard_1_data));  // open: re, clr
  // ROM #(.addrWidth(12), .line("quad")) rom_1: pin names not known
  assign bit_extender_1_out = {{25{1'b0}}, keyboard_1_data};  // Bit_Extender bit_extender_1
  assign bit_extender_2_out = {{31{1'b0}}, keyboard_1_avail};  // Bit_Extender bit_extender_2
  Multiplexer #(.width(32)) multiplexer_4 (.in0(immS), .in1(valRb), .out(multiplexer_4_out), .sel(smx1));
  RAM #(.addrWidth(13), .clearpin("true")) ram_1 (
    .addr(subtractor_1_out[12:0]), .we(and_1_out), .oe(1'b1), .clk(C), .din(valRb[7:0]), .dout(valMem[7:0]),
    .clr(R));
  Multiplexer #(.width(32)) multiplexer_5 (
    .in0(valMem), .in1(bit_extender_1_out), .out(multiplexer_5_out), .sel(comparator_2_eq));
  Multiplexer #(.width(32)) multiplexer_6 (
    .in0(multiplexer_5_out), .in1(bit_extender_2_out), .out(valData), .sel(comparator_3_eq));
  assign immNs = {{16{1'b0}}, {numRd, undriven_2, undriven, Nf}};  // Bit_Extender bit_extender_3
  assign immS = {{16{numRd[4]}}, {numRd, undriven_2, undriven, Nf}};  // Bit_Extender bit_extender_4
  assign Shamt = {{27{1'b0}}, {undriven_2, undriven}};  // Bit_Extender bit_extender_5
  UAL ual_1 (.A(banc_reg_1_valrs), .B(multiplexer_4_out), .Op(Op), .S(resUAL), .zero(ual_1_zero));
  and and_3 (and_3_out, ual_1_zero, sbeq);
  and and_4 (and_4_out, ~ual_1_zero, sbne);  // AND_Gate
  or or_1 (mxBr, and_3_out, and_4_out);
  CMD cmd_1 (
    .Co(Co), .Nf(Nf), .sjal(sjal), .sbeq(sbeq), .sbne(sbne), .Op(Op), .sjr(sjr), .slbu(slbu), .ssb(ssb),
    .smx1(smx1), .sNs(sNs), .sShamt(sShamt), .serg(sereg));

  // Notes on the sheet:
  //   Calcul cp suivant
  //   Console clavier et écran
  //   contents of rom_1 (hex, n*v repeats v):
  //   5 0 4 24 ff ff 5 24 21 20 85 0 30 0 86 24 c 7f 6 a0 fc ff 80 14 f9 ff 0 10
  //   Chemin de données UAL
  //   Mémoire de données
  //   Décodage instruction
  //   Condition de branchement
  //   Commande du système
endmodule

// MIPS_CPL
module MIPS_COMPLET (
  output [31:0] cpp4,
  output [31:0] ssl2,
  output [31:0] valRs
);

  wire and_1_out, and_2_out, and_3_out, C, comparator_1_eq, comparator_2_eq, comparator_3_eq,
       comparator_4_lt, keyboard_1_avail, mxBr, not_1_out, q1, q3, q6, q8, q11, R, rgb_video_1_p3,
       rgb_video_1_p5, rgb_video_1_p7, rgb_video_1_p9, sbeq, sbne, sereg, sjal, sjr, slbu, smx1, sNs, ssb,
       sShamt, ual_1_zero;
  wire [2:0] undriven_3;
  wire [3:0] Op;
  wire [4:0] multiplexer_3_out, multiplexer_4_out, numRd, numRs, numRt, undriven;
  wire [5:0] Co, Nf;
  wire [6:0] keyboard_1_data;
  wire [7:6] undriven_2;
  wire [31:0] adder_2_out, banc_reg_1_val_a0, banc_reg_1_val_a1, banc_reg_1_val_a2, banc_reg_1_val_a3,
       banc_reg_1_val_ra, banc_reg_1_val_v0, banc_reg_1_val_v1, bit_extender_1_out, bit_extender_2_out,
       immNs, immS, multiplexer_1_out, multiplexer_2_out, multiplexer_5_out, multiplexer_6_out,
       multiplexer_7_out, multiplexer_8_out, multiplexer_9_out, multiplexer_10_out, multiplexer_11_out, q0,
       q2, q4, q7, q9, q10, register_1_q, resUAL, Shamt, subtractor_1_out, valData, valMem, valRb;

  Clock clock_1 (.out(C));
  Shifter #(.width(32)) shifter_1 (.in(immS), .\dist (5'b00010), .out(ssl2));
  Multiplexer #(.width(32)) multiplexer_1 (.in0(resUAL), .in1(valData), .out(multiplexer_1_out), .sel(slbu));
  Adder #(.width(32)) adder_1 (.a(register_1_q), .b(32'h4), .out(cpp4));  // open: cin, cout
  Adder #(.width(32)) adder_2 (.a(cpp4), .b(ssl2), .out(adder_2_out));  // open: cin, cout
  Multiplexer #(.width(32)) multiplexer_2 (.in0(multiplexer_1_out), .in1(q4), .out(multiplexer_2_out), .sel(q1));
  Multiplexer #(.width(5)) multiplexer_3 (.in0(numRt), .in1(numRd), .out(multiplexer_3_out), .sel(smx1));
  Multiplexer #(.width(5)) multiplexer_4 (.in0(multiplexer_3_out), .in1(undriven), .out(multiplexer_4_out), .sel(q6));
  Multiplexer #(.width(32)) multiplexer_5 (.in0(cpp4), .in1(adder_2_out), .out(multiplexer_5_out), .sel(mxBr));
  Multiplexer #(.width(32)) multiplexer_6 (.in0(multiplexer_5_out), .in1(q0), .out(multiplexer_6_out), .sel(q1));
  Comparator #(.mode("unsigned"), .width(32)) comparator_1 (
    .a(resUAL), .b(32'h7f0c), .eq(comparator_1_eq));  // open: gt, lt
  Comparator #(.mode("unsigned"), .width(32)) comparator_2 (
    .a(resUAL), .b(32'h7f04), .eq(comparator_2_eq));  // open: gt, lt
  Comparator #(.mode("unsigned"), .width(32)) comparator_3 (
    .a(resUAL), .b(32'h7f00), .eq(comparator_3_eq));  // open: gt, lt
  POR #(.PorHighDuration(1)) por_1 (.out(R));
  Multiplexer #(.width(32)) multiplexer_7 (.in0(multiplexer_6_out), .in1(q2), .out(multiplexer_7_out), .sel(q3));
  Subtractor #(.width(32)) subtractor_1 (.a(resUAL), .b(32'h2000), .out(subtractor_1_out));  // open: bin, bout
  Comparator #(.mode("unsigned"), .width(32)) comparator_4 (
    .a(subtractor_1_out), .b(32'h2000), .lt(comparator_4_lt));  // open: gt, eq
  Register #(.width(32)) register_1 (.D(multiplexer_7_out), .en(1'b1), .Q(register_1_q), .clk(not_1_out), .clr(R));
  not not_1 (not_1_out, C);
  BANC_REG banc_reg_1 (
    .ValRw(multiplexer_2_out), .H(C), .numRs(numRs), .numRt(numRt), .ereg(sereg), .numRw(multiplexer_4_out),
    .valRs(valRs), .valRt(valRb), .val_v0(banc_reg_1_val_v0), .val_v1(banc_reg_1_val_v1),
    .val_a0(banc_reg_1_val_a0), .val_a1(banc_reg_1_val_a1), .val_a2(banc_reg_1_val_a2),
    .val_a3(banc_reg_1_val_a3), .val_ra(banc_reg_1_val_ra));
  // Probe on banc_reg_1_val_v0
  // Probe on banc_reg_1_val_v1
  // Probe on banc_reg_1_val_a0
  // Probe on banc_reg_1_val_a1
  // Probe on banc_reg_1_val_a2
  // Probe on banc_reg_1_val_a3
  // Probe on banc_reg_1_val_ra
  and and_1 (and_1_out, comparator_4_lt, ssb);
  TTY tty_1 (.data(valRb[6:0]), .clk(C), .we(comparator_1_eq), .clr(R));
  Keyboard keyboard_1 (.clk(C), .re(comparator_2_eq), .clr(R), .avail(keyboard_1_avail), .data(keyboard_1_data));
  // ROM #(.addrWidth(12), .line("quad")) rom_1: pin names not known
  Multiplexer #(.width(32)) multiplexer_8 (.in0(valRs), .in1(q7), .out(multiplexer_8_out), .sel(q8));
  Multiplexer #(.width(32)) multiplexer_9 (.in0(q9), .in1(q10), .out(multiplexer_9_out), .sel(q11));
  assign bit_extender_1_out = {{25{1'b0}}, keyboard_1_data};  // Bit_Extender bit_extender_1
  assign bit_extender_2_out = {{31{1'b0}}, keyboard_1_avail};  // Bit_Extender bit_extender_2
  Multiplexer #(.width(32)) multiplexer_10 (.in0(multiplexer_9_out), .in1(valRb), .out(multiplexer_10_out), .sel(smx1));
  RAM #(.addrWidth(13), .clearpin("true")) ram_1 (
    .addr(subtractor_1_out[12:0]), .we(and_1_out), .oe(1'b1), .clk(C), .din(valRb[7:0]), .dout(valMem[7:0]),
    .clr(R));
  Multiplexer #(.width(32)) multiplexer_11 (
    .in0(valMem), .in1(bit_extender_1_out), .out(multiplexer_11_out), .sel(comparator_2_eq));
  Multiplexer #(.width(32)) multiplexer_12 (
    .in0(multiplexer_11_out), .in1(bit_extender_2_out), .out(valData), .sel(comparator_3_eq));
  assign immNs = {{16{1'b0}}, {numRd, undriven_3, undriven_2, Nf}};  // Bit_Extender bit_extender_3
  assign immS = {{16{numRd[4]}}, {numRd, undriven_3, undriven_2, Nf}};  // Bit_Extender bit_extender_4
  assign Shamt = {{27{1'b0}}, {undriven_3, undriven_2}};  // Bit_Extender bit_extender_5
  UAL ual_1 (.A(multiplexer_8_out), .B(multiplexer_10_out), .Op(Op), .S(resUAL), .zero(ual_1_zero));
  and and_2 (and_2_out, ual_1_zero, sbeq);
  and and_3 (and_3_out, ~ual_1_zero, sbne);  // AND_Gate
  // RGB_Video #(.cursor("No Cursor"), .height(16), .scale(8), .width(16)) rgb_video_1: pin names not known; wires that end beside it: R, C, rgb_video_1_p3, rgb_video_1_p3, rgb_video_1_p5, rgb_video_1_p5, rgb_video_1_p7, rgb_video_1_p7, rgb_video_1_p9, rgb_video_1_p9
  or or_1 (mxBr, and_2_out, and_3_out);
  CMD cmd_1 (
    .Co(Co), .Nf(Nf), .sjal(sjal), .sbeq(sbeq), .sbne(sbne), .Op(Op), .sjr(sjr), .slbu(slbu), .ssb(ssb),
    .smx1(smx1), .sNs(sNs), .sShamt(sShamt), .serg(sereg));

  // Notes on the sheet:
  //   Calcul cp suivant
  //   q5
  //   Console clavier et écran
  //   contents of rom_1 (hex, n*v repeats v):
  //   5 0 4 24 ff ff 5 24 21 20 85 0 30 0 86 24 c 7f 6 a0 fc ff 80 14 f9 ff 0 10
  //   Chemin de données UAL
  //   Mémoire de données
  //   Décodage instruction
  //   Affichage 16x16
  //   Condition de branchement
  //   Commande du système
endmodule

module PGM (
);


  // Notes on the sheet:
  //   .text boucle: boucle2: lbu $a0,0x7F00($0) beq $a0,$0,boucle lbu $a0,0x7F04($0) sb $a0,0x7F0C($0) beq $0,$0,boucle
  //   PGM3 Ecran Blanc
  //   .text addiu $a0,$0,-1 boucle: sb $a0,0x7F20($0) andi $a1,$a0,0xFF addiu $a0,$a0,-1 bne $a1,$0,boucle
  //   PGM4 Fonctions
  //   .text jal lecture jal affichage  fin: beq $0,$0,fin lecture: lbu $a0,0x7F00($0) beq $a0,$0,lecture lbu $a0,0x7F04($0) sb $a0,0x7F0C($0) jr $ra
  //   affichage: addiu $a0,$0,-1 affichage_boucle: sb $a0,0x7F20($0) andi $a1,$a0,0xFF addiu $a0,$a0,-1 bne $a1,$0,affichage_boucle jr $ra
  //   PGM1 Itération
  //   PGM2 Entrée /sortie Console
  //   .text boucle: addiu $a0,$0,5 addiu $a1,$0,-1 boucle2: addu $a0,$a0,$a1 addiu $a2,$a0,'0' sb $a2,0x7F0C($0) bne $a0,$0,boucle2 beq $0,$0,boucle
endmodule
